# Fritzing sketch main (saved by Fritzing 0.9.2b)
circuit board: 8.52876cm x 5.6388cm
breadboards: 1

parts:
  U1 = atmega328 [package=dip]
  Raspberry_Pi_2 = Raspberry Pi 2
  Port3 = shrouded pin header, 6 pins [form="♂ (shrouded male)"]
  Port2 = shrouded pin header, 6 pins [form="♂ (shrouded male)"]
  Port1 = shrouded pin header, 6 pins [form="♂ (shrouded male)"]
  GPS = female pin header, 9 pins [form="♀ (female)"]
  M2 = male pin header, 2 pins [form="♂ (male)"]
  M3 = male pin header, 2 pins [form="♂ (male)"]
  M4 = male pin header, 2 pins [form="♂ (male)"]
  M1 = male pin header, 2 pins [form="♂ (male)"]
  A3 = male pin header, 3 pins [form="♂ (male)"]
  A2 = male pin header, 3 pins [form="♂ (male)"]
  A1 = male pin header, 3 pins [form="♂ (male)"]
  ISP = double row female pin header, 6 pins [form="♀ (female)"]
  A0 = male pin header, 3 pins [form="♂ (male)"]
  J1 = female pin header, 2 pins [form="♀ (female)"]
  J2 = female pin header, 2 pins [form="♀ (female)"]
  Disp = male pin header, 3 pins [form="♂ (male)"]
  Port4 = shrouded pin header, 6 pins [form="♂ (shrouded male)"]
  IC1 = SSOP20 [chip_label=74LVC244 package=SSOP]
  R1 = Resistor [tolerance=±1% resistance=10k package="0805 [SMD]"]
  R2 = Resistor [tolerance=±1% resistance=100k package="0805 [SMD]"]
  R3 = Resistor [tolerance=±1% resistance=10k package="0805 [SMD]"]
  R4 = Resistor [tolerance=±1% resistance=10k package="0805 [SMD]"]
  R7 = Resistor [tolerance=±1% resistance=10k package="0805 [SMD]"]
  R6 = Resistor [tolerance=±1% resistance=10k package="0805 [SMD]"]
  R5 = Resistor [tolerance=±1% resistance=10k package="0805 [SMD]"]
  C4 = Ceramic Capacitor [capacitance=100nF package="0805 [SMD, multilayer]"]
  C3 = Ceramic Capacitor [capacitance=100nF package="0805 [SMD, multilayer]"]
  C2 = Ceramic Capacitor [capacitance=22pF package="0805 [SMD, multilayer]"]
  C1 = Ceramic Capacitor [capacitance=22pF package="0805 [SMD, multilayer]"]
  Q3 = MOSFET-NCHANNEL [package=sot23-3]
  Q2 = MOSFET-NCHANNEL [package=sot23-3]
  Q1 = MOSFET-NCHANNEL [package=sot23-3]
  XTAL1 = Crystal [frequency="16 Mhz" package=THT]
  U3 = LT3514 [package=tssop-24]  # not connected

nets:
  AVR_RST: U1.RESET, ISP.pin3, R3.Pin_1, Q1.D
  AVR_RX: U1.D0_(RX), J2.pin2
  AVR_TX: U1.D1_(TX), J1.pin2
  AVR_D2: U1.D2, M1.pin1
  PWM0: U1.D3_(PWM), M1.pin2
  AVR_D4: U1.D4, M2.pin1
  5V: U1.VCC, U1.AVCC, Port3.pin1, Port2.pin1, Port1.pin1, A3.pin2, A2.pin2, A1.pin2, ISP.pin6, A0.pin2, Disp.pin2, Port4.pin1, R3.Pin_0, R7.Pin_1, R6.Pin_1, C4.0, C3.1
  GND: U1.GND, Raspberry_Pi_2.GND, Port3.pin3, Port3.pin6, Port2.pin3, Port2.pin6, Port1.pin3, Port1.pin6, GPS.pin7, A3.pin3, A2.pin3, A1.pin3, ISP.pin4, A0.pin3, Disp.pin3, Port4.pin3, Port4.pin6, IC1.10, IC1.11, IC1.13, IC1.15, IC1.17, R2.Pin_0, C4.1, C3.0, C2.1, C1.1, Q1.S
  N1: U1.XLAT1, C2.0, XTAL1.pin_1
  N2: U1.XLAT2, C1.0, XTAL1.pin_0
  PWM1: U1.D5_(PWM), M2.pin2
  PWM2: U1.D6_(PWM), M3.pin2
  AVR_D7: U1.D7, M3.pin1
  AVR_D8: U1.D8, M4.pin1
  PWM3: U1.D9_(PWM), M4.pin2
  N3: U1.D10_(PWM), Disp.pin1
  AVR_MOSI: U1.D11_(PWM), ISP.pin5, IC1.14
  AVR_MISO: U1.D12, ISP.pin1, IC1.8
  AVR_SCK: U1.D13, ISP.pin2, IC1.16
  ADC0: U1.A0, A0.pin1
  ADC1: U1.A1, A1.pin1
  ADC2: U1.A2, A2.pin1
  ADC3: U1.A3, A3.pin1
  5V_SDA: U1.A4, Port3.pin4, Port2.pin4, Port1.pin4, Port4.pin4, R7.Pin_0, Q2.D
  5V_SCL: U1.A5, Port3.pin5, Port2.pin5, Port1.pin5, Port4.pin5, R6.Pin_0, Q3.D
  3.3V_SDA: Raspberry_Pi_2.GPIO2, R4.Pin_0, Q2.S
  3.3V_SCL: Raspberry_Pi_2.GPIO3, R5.Pin_0, Q3.S
  PI_MOSI: Raspberry_Pi_2.GPIO10, IC1.6
  PI_MISO: Raspberry_Pi_2.GPIO9, IC1.12
  PI_SCK: Raspberry_Pi_2.GPIO11, IC1.4
  N4: Raspberry_Pi_2.GPIO26, GPS.pin2
  PI_CE0: Raspberry_Pi_2.GPIO8, IC1.1, R1.Pin_0
  N5: Raspberry_Pi_2.GPIO15, GPS.pin5, J2.pin1
  N6: Raspberry_Pi_2.GPIO14, GPS.pin6, J1.pin1
  3.3V: Port3.pin2, Port2.pin2, Port1.pin2, GPS.pin1, Port4.pin2, IC1.19, IC1.20, R1.Pin_1, R4.Pin_1, R5.Pin_1, Q3.G, Q2.G
  N7: R2.Pin_1, Q1.G

notes:
  3.3V
  VBAT
  FIX
  TX
  RX
  GND
  VIN
  PPS
  EN
  I2C Level Shifter
  Raspberry Pi Header
  Atmel ATMEGA 328p
  ATMEGA Programmer
  ADC Header
  Expansion Ports
  Motors
  5V
  G
  A
  Rx
  E
  Pathfinder v2
  ○
  Andy Condon ©2016
  M

custom parts:
  LT3514: Linear Technology LT3514 Triple Step-Down Switching Regulator Three Outputs: 2A, 1A, 1A
