# Fritzing sketch navigator (saved by Fritzing 0.9.2b)
breadboards: 1

parts:
  U1 = atmega328 [package=dip]  # not connected
  Raspberry_Pi_2 = Raspberry Pi 2
  GPS1 = Adafruit Ultimate GPS Breakout
  XTAL1 = Crystal [frequency="16 Mhz" package=THT]  # not connected
  IC1 = IC, DIP package, 20 pins [chip_label=IC]  # not connected

nets:
  3V3: Raspberry_Pi_2.3V3, GPS1.3.3V
  GND: Raspberry_Pi_2.GND, GPS1.GND
  N1: Raspberry_Pi_2.GPIO15, GPS1.TX
  N2: Raspberry_Pi_2.GPIO14, GPS1.RX
